# Fritzing sketch dcMotor2StepperControl-Sketch 2 (saved by Fritzing 0.9.3b)

parts:
  Part1 = Arduino Mega 2560 (Rev3)
  JP2 = Header 4 [part_number="Step/Dir X & Y" package=jst-4-pth]
  S1 = H-Bridge with L298N
  DC_Mot_Enc1 = DC Motor with two-phase hall-encoder [part_number=VT-E-G25A-06-177E]
  DC_Mot_Enc2 = DC Motor with two-phase hall-encoder [part_number=VT-E-G25A-06-177E]

nets:
  N1: Part1.D21/SCL, JP2.3
  N2: Part1.D20/SDA, DC_Mot_Enc1.pin3
  N3: Part1.D19/RX1, JP2.1
  N4: Part1.D18/TX1, DC_Mot_Enc2.pin3
  N5: Part1.D8_PWM, S1.IN4
  N6: Part1.3V3, DC_Mot_Enc1.pin5, DC_Mot_Enc2.pin5
  N7: Part1.GND, DC_Mot_Enc1.pin2, DC_Mot_Enc2.pin2
  N8: Part1.D3_PWM, S1.ENA
  N9: Part1.D4_PWM, S1.ENB
  N10: Part1.D5_PWM, S1.IN1
  N11: Part1.D6_PWM, S1.IN2
  N12: Part1.D7_PWM, S1.IN3
  N13: Part1.D22, DC_Mot_Enc2.pin4
  N14: Part1.D23, JP2.2
  N15: Part1.D25, JP2.4
  N16: S1.M1-01, DC_Mot_Enc1.pin1
  N17: S1.M1-02, DC_Mot_Enc1.pin6
  N18: S1.M2-01, DC_Mot_Enc2.pin6
  N19: S1.M2-02, DC_Mot_Enc2.pin1

custom parts:
  H-Bridge with L298N: h-bridge
